# Fritzing sketch Circuit (saved by Fritzing 0.9.2b)
breadboards: 1

parts:
  DHT22 = Humidity and Temperature Sensor RHT03
  BMP280 = Barometric Pressure Sensor - BMP085 Breakout
  Photoresistor = PHOTOCELL [package=photocell]
  To_ESP8266_pins = Header 6 [package=1x06-smd]
  part = Resistor [tolerance=±5% resistance=10k package="1206 [SMD]"]
  part_2 = DC Power [voltage=3.3V]

nets:
  VCC: DHT22.Vcc, BMP280.VCC, To_ESP8266_pins.1, part_2.V+
  N1: DHT22.Data-signal, To_ESP8266_pins.4
  GND: DHT22.GND_2, BMP280.GND, part.Pin_0, part_2.V-
  N2: BMP280.SCL, To_ESP8266_pins.2
  N3: BMP280.SDA, To_ESP8266_pins.3
  N4: Photoresistor.P$1, To_ESP8266_pins.6
  N5: Photoresistor.P$2, part.Pin_1
